// Digital circuit ADDI.dig as structural Verilog
module ADDI (
  input  [6:0] iw_opcode,
  input  [6:0] opcode,
  input  [2:0] iw_funct3,
  input  [2:0] funct3,
  output eq
);

  wire comparator_1_eq, comparator_2_eq;

  Comparator #(.Bits(7)) comparator_1 (.a(iw_opcode), .b(opcode), .eq(comparator_1_eq));  // open: gt, lt
  Comparator #(.Bits(3)) comparator_2 (.a(iw_funct3), .b(funct3), .eq(comparator_2_eq));  // open: gt, lt
  and and_1 (eq, comparator_1_eq, comparator_2_eq);
endmodule
