// Digital circuit branch-unit.dig as structural Verilog
module branch_unit (
  input  [63:0] RD0,
  input  [63:0] RD1,
  input  PCsel,
  input  [2:0] BROp,
  output PCbr
);

  wire beq_eq, bge_eq, bge_gt, blt_lt, bne_eq, not_1_out, or_1_out, or_2_out, or_3_out, or_4_out, or_5_out;

  Comparator #(.Bits(64)) beq (.a(RD0), .b(RD1), .eq(beq_eq));  // open: gt, lt
  Comparator #(.Bits(64)) bne (.a(RD0), .b(RD1), .eq(bne_eq));  // open: gt, lt
  Comparator #(.Bits(64)) blt (.a(RD0), .b(RD1), .lt(blt_lt));  // open: gt, eq
  Comparator #(.Bits(64)) bge (.a(RD0), .b(RD1), .gt(bge_gt), .eq(bge_eq));  // open: lt
  not not_1 (not_1_out, bne_eq);
  or or_1 (or_1_out, bge_gt, bge_eq);
  or or_2 (or_2_out, PCsel, beq_eq);
  or or_3 (or_3_out, PCsel, not_1_out);
  or or_4 (or_4_out, PCsel, blt_lt);
  or or_5 (or_5_out, PCsel, or_1_out);
  Multiplexer #(.Selector_Bits(3)) multiplexer_1 (
    .sel(BROp), .in_0(PCsel), .in_1(or_2_out), .in_2(or_3_out), .in_3(or_4_out), .in_4(or_5_out),
    .in_5(1'b0), .in_6(1'b0), .in_7(1'b0), .out(PCbr));
endmodule
