// Digital circuit instruction-decoder.dig as structural Verilog
module instruction_decoder (
  input  [31:0] IW,
  output WDsel,
  output [3:0] ALUOp,
  output RFW,
  output PCsel,
  output [2:0] ALUSrcB,
  output ALUSrcA,
  output [2:0] BROp,
  output M2R,
  output LD,
  output ST,
  output [1:0] MSZ
);

  wire addi_eq, addr_eq, andi_eq, andiw_eq, andr_eq, beq_eq, bge_eq, blt_eq, bne_eq, jal_eq, jalr_eq, lb_eq,
       ld_eq, lui_eq, lw_eq, mul_eq, or_eq, ori_eq, sb_eq, sd_eq, sll_eq, slli_eq, sra_eq, srai_eq, srl_eq,
       srli_eq, subr_eq, sw_eq;
  wire [4:0] INUM_num;

  ADDI addi (.iw_opcode(IW[6:0]), .opcode(7'b0010011), .iw_funct3(IW[14:12]), .funct3(3'b000), .eq(addi_eq));
  ADDR addr (
    .iw_opcode(IW[6:0]), .opcode(7'b0110011), .iw_funct3(IW[14:12]), .funct3(3'b000), .iw_funct7(IW[31:25]),
    .funct7({7{1'b0}}), .eq(addr_eq));
  Comparator #(.Bits(7)) jal (.a(IW[6:0]), .b(7'b1101111), .eq(jal_eq));  // open: gt, lt
  ADDI jalr (.iw_opcode(IW[6:0]), .opcode(7'b1100111), .iw_funct3(IW[14:12]), .funct3(3'b000), .eq(jalr_eq));
  ADDI beq (.iw_opcode(IW[6:0]), .opcode(7'b1100011), .iw_funct3(IW[14:12]), .funct3(3'b000), .eq(beq_eq));
  ADDI bne (.iw_opcode(IW[6:0]), .opcode(7'b1100011), .iw_funct3(IW[14:12]), .funct3(3'b001), .eq(bne_eq));
  ADDI blt (.iw_opcode(IW[6:0]), .opcode(7'b1100011), .iw_funct3(IW[14:12]), .funct3(3'b100), .eq(blt_eq));
  ADDI bge (.iw_opcode(IW[6:0]), .opcode(7'b1100011), .iw_funct3(IW[14:12]), .funct3(3'b101), .eq(bge_eq));
  ADDR subr (
    .iw_opcode(IW[6:0]), .opcode(7'b0110011), .iw_funct3(IW[14:12]), .funct3(3'b000), .iw_funct7(IW[31:25]),
    .funct7(7'b0100000), .eq(subr_eq));
  ADDR sll (
    .iw_opcode(IW[6:0]), .opcode(7'b0110011), .iw_funct3(IW[14:12]), .funct3(3'b001), .iw_funct7(IW[31:25]),
    .funct7({7{1'b0}}), .eq(sll_eq));
  ADDR srl (
    .iw_opcode(IW[6:0]), .opcode(7'b0110011), .iw_funct3(IW[14:12]), .funct3(3'b101), .iw_funct7(IW[31:25]),
    .funct7({7{1'b0}}), .eq(srl_eq));
  ADDR sra (
    .iw_opcode(IW[6:0]), .opcode(7'b0110011), .iw_funct3(IW[14:12]), .funct3(3'b101), .iw_funct7(IW[31:25]),
    .funct7(7'b0100000), .eq(sra_eq));
  ADDR mul (
    .iw_opcode(IW[6:0]), .opcode(7'b0110011), .iw_funct3(IW[14:12]), .funct3(3'b000), .iw_funct7(IW[31:25]),
    .funct7(7'b0000001), .eq(mul_eq));
  SLLI slli (
    .iw_opcode(IW[6:0]), .opcode(7'b0010011), .iw_funct3(IW[14:12]), .funct3(3'b001), .iw_funct6(IW[31:26]),
    .funct6({6{1'b0}}), .eq(slli_eq));
  SLLI srli (
    .iw_opcode(IW[6:0]), .opcode(7'b0010011), .iw_funct3(IW[14:12]), .funct3(3'b101), .iw_funct6(IW[31:26]),
    .funct6({6{1'b0}}), .eq(srli_eq));
  SLLI srai (
    .iw_opcode(IW[6:0]), .opcode(7'b0010011), .iw_funct3(IW[14:12]), .funct3(3'b101), .iw_funct6(IW[31:26]),
    .funct6(6'b010000), .eq(srai_eq));
  ADDI u_ld (.iw_opcode(IW[6:0]), .opcode(7'b0000011), .iw_funct3(IW[14:12]), .funct3(3'b011), .eq(ld_eq));
  ADDI sd (.iw_opcode(IW[6:0]), .opcode(7'b0100011), .iw_funct3(IW[14:12]), .funct3(3'b011), .eq(sd_eq));
  ADDI lw (.iw_opcode(IW[6:0]), .opcode(7'b0000011), .iw_funct3(IW[14:12]), .funct3(3'b010), .eq(lw_eq));
  ADDI sw (.iw_opcode(IW[6:0]), .opcode(7'b0100011), .iw_funct3(IW[14:12]), .funct3(3'b010), .eq(sw_eq));
  ADDI lb (.iw_opcode(IW[6:0]), .opcode(7'b0000011), .iw_funct3(IW[14:12]), .funct3(3'b000), .eq(lb_eq));
  ADDI sb (.iw_opcode(IW[6:0]), .opcode(7'b0100011), .iw_funct3(IW[14:12]), .funct3(3'b000), .eq(sb_eq));
  ADDR \or  (
    .iw_opcode(IW[6:0]), .opcode(7'b0110011), .iw_funct3(IW[14:12]), .funct3(3'b110), .iw_funct7(IW[31:25]),
    .funct7({7{1'b0}}), .eq(or_eq));
  ADDR andr (
    .iw_opcode(IW[6:0]), .opcode(7'b0110011), .iw_funct3(IW[14:12]), .funct3(3'b111), .iw_funct7(IW[31:25]),
    .funct7({7{1'b0}}), .eq(andr_eq));
  ADDI ori (.iw_opcode(IW[6:0]), .opcode(7'b0010011), .iw_funct3(IW[14:12]), .funct3(3'b110), .eq(ori_eq));
  ADDI andi (.iw_opcode(IW[6:0]), .opcode(7'b0010011), .iw_funct3(IW[14:12]), .funct3(3'b111), .eq(andi_eq));
  ADDI andiw (.iw_opcode(IW[6:0]), .opcode(7'b0011011), .iw_funct3(IW[14:12]), .funct3(3'b000), .eq(andiw_eq));
  Comparator #(.Bits(7)) lui (.a(IW[6:0]), .b(7'b0110111), .eq(lui_eq));  // open: gt, lt
  PriorityEncoder #(.Selector_Bits(5)) INUM (
    .in0(addi_eq), .in1(addr_eq), .in2(jal_eq), .in3(jalr_eq), .in4(beq_eq), .in5(bne_eq), .in6(blt_eq),
    .in7(bge_eq), .in8(subr_eq), .in9(sll_eq), .in10(srl_eq), .in11(sra_eq), .in12(mul_eq), .in13(slli_eq),
    .in14(srli_eq), .in15(srai_eq), .in16(lui_eq), .in17(ld_eq), .in18(sd_eq), .in19(lw_eq), .in20(sw_eq),
    .in21(lb_eq), .in22(sb_eq), .in23(or_eq), .in24(andr_eq), .in25(ori_eq), .in26(andi_eq), .in27(andiw_eq),
    .in28(1'b0), .in29(1'b0), .in30(1'b0), .in31(1'b0), .num(INUM_num));  // open: any
  ROM #(.AddrBits(5), .Bits(19)) rom_1 (
    .A(INUM_num), .sel(1'b1), .D({MSZ, ST, LD, M2R, BROp, RFW, ALUOp, ALUSrcA, ALUSrcB, PCsel, WDsel}));

  // Other names for the same wires on the sheet: opcode[6:0] = IW[6:0]; funct3[2:0] = IW[14:12];
  //   funct7[6:0] = IW[31:25]; funct6[5:0] = IW[31:26]

  // Notes on the sheet:
  //   contents of rom_1 (hex, n*v repeats v):
  //   404,400,437,407,82c,102c,182c,202c,440,4c0,500,540,480,4c4,504
  //   ,544,410,6c404,7c008,4c404,5c008,c404,1c008,580,5c0,584,5c4,604
endmodule
