// Digital circuit project06.dig as structural Verilog
module project06 (
  input  CLK,
  input  CLR,
  input  [4:0] PROG,
  input  EN,
  output DONE,
  output [63:0] zero,
  output [63:0] ra,
  output [63:0] T0,
  output [63:0] sp,
  output [63:0] gp,
  output [63:0] tp,
  output [63:0] s1,
  output [63:0] T1,
  output [63:0] T2,
  output [63:0] s0_fp,
  output [63:0] A3,
  output [63:0] A0,
  output [63:0] A1,
  output [63:0] A2,
  output [63:0] A4,
  output [63:0] A5,
  output [63:0] A6,
  output [63:0] s4,
  output [63:0] A7,
  output [63:0] s2,
  output [63:0] s3,
  output [63:0] s8,
  output [63:0] s5,
  output [63:0] s6,
  output [63:0] s7,
  output [63:0] T3,
  output [63:0] s9,
  output [63:0] s10,
  output [63:0] s11,
  output [63:0] T4,
  output [63:0] T6,
  output [63:0] T5,
  output [63:0] PC,
  output [31:0] IW,
  output [4:0] RS1,
  output [4:0] RS2,
  output [4:0] RD,
  output [63:0] Imm_I,
  output [1:0] TYPE_OF_STORE_LOAD
);

  wire ALUSrcA, and_2_out, CLK_t, LD, M2R, PCbr, PCsel, RFW, ST, WDsel;
  wire [2:0] ALUSrcB, BROp;
  wire [3:0] ALUOp;
  wire [63:0] alu_1_r, Dcur, immediate_decoder_1_imm_b, immediate_decoder_1_imm_j, immediate_decoder_1_imm_s,
       immediate_decoder_1_imm_u, immediate_decoder_1_shamt, load_unit_1_dcur, multiplexer_1_out,
       multiplexer_2_out, multiplexer_3_out, multiplexer_4_out, multiplexer_5_out, PC_plus_4_s,
       register_file_1_rd0, register_file_1_rd1, store_unit_1_d;

  Multiplexer #(.Bits(64)) multiplexer_1 (
    .sel(PCbr), .in_0(PC_plus_4_s), .in_1(multiplexer_5_out), .out(multiplexer_1_out));
  and and_1 (CLK_t, CLK, ~DONE);  // And
  Comparator #(.Bits(32)) End (.a(IW), .b(32'hc0001073), .eq(DONE));  // open: gt, lt
  _64_bit_register_w_clr _64_bit_register_w_clr_1 (.D(multiplexer_1_out), .CLK(CLK_t), .EN(EN), .CLR(CLR), .Q(PC));
  LED led_1 (.in(DONE));
  // inst_mem inst_mem_1: pin names not known; wires that end beside it: PROG, PC[9:2], IW
  Add #(.Bits(64)) PC_plus_4 (.a(PC), .b(64'h4), .c_i(1'b0), .s(PC_plus_4_s));  // open: c_o
  immediate_decoder immediate_decoder_1 (
    .IW(IW), .imm_I(Imm_I), .imm_S(immediate_decoder_1_imm_s), .imm_B(immediate_decoder_1_imm_b),
    .imm_U(immediate_decoder_1_imm_u), .imm_J(immediate_decoder_1_imm_j), .shamt(immediate_decoder_1_shamt));
  instruction_decoder instruction_decoder_1 (
    .IW(IW), .WDsel(WDsel), .PCsel(PCsel), .ALUSrcB(ALUSrcB), .ALUSrcA(ALUSrcA), .ALUOp(ALUOp), .RFW(RFW),
    .BROp(BROp), .M2R(M2R), .LD(LD), .ST(ST), .MSZ(TYPE_OF_STORE_LOAD));
  register_decoder register_decoder_1 (.IW(IW), .RS1(RS1), .RS2(RS2), .RD(RD));
  and and_2 (and_2_out, RFW, EN);
  Multiplexer #(.Bits(64)) multiplexer_2 (
    .sel(WDsel), .in_0(multiplexer_5_out), .in_1(PC_plus_4_s), .out(multiplexer_2_out));
  register_file register_file_1 (
    .RR0(RS1), .RR1(RS2), .WE(and_2_out), .WR(RD), .WD(multiplexer_2_out), .CLK(CLK_t), .CLR(CLR), .x31(T6),
    .x30(T5), .x29(T4), .x28(T3), .x27(s11), .x26(s10), .x25(s9), .x24(s8), .x23(s7), .x22(s6), .x21(s5),
    .x20(s4), .x19(s3), .x18(s2), .x17(A7), .x16(A6), .x15(A5), .x14(A4), .x13(A3), .x12(A2), .x11(A1),
    .x10(A0), .x9(s1), .x8(s0_fp), .x7(T2), .x6(T1), .x5(T0), .x4(tp), .x3(gp), .x2(sp), .x1(ra), .x0(zero),
    .RD0(register_file_1_rd0), .RD1(register_file_1_rd1));
  branch_unit branch_unit_1 (
    .RD0(register_file_1_rd0), .RD1(register_file_1_rd1), .PCsel(PCsel), .BROp(BROp), .PCbr(PCbr));
  Multiplexer #(.Selector_Bits(3), .Bits(64)) multiplexer_3 (
    .sel(ALUSrcB), .in_0(register_file_1_rd1), .in_1(Imm_I), .in_2(immediate_decoder_1_imm_s),
    .in_3(immediate_decoder_1_imm_b), .in_4(immediate_decoder_1_imm_u), .in_5(immediate_decoder_1_imm_j),
    .in_6(immediate_decoder_1_shamt), .in_7({64{1'b0}}), .out(multiplexer_3_out));
  Multiplexer #(.Bits(64)) multiplexer_4 (
    .sel(ALUSrcA), .in_0(register_file_1_rd0), .in_1(PC), .out(multiplexer_4_out));
  alu alu_1 (.A(multiplexer_4_out), .B(multiplexer_3_out), .ALUOp(ALUOp), .R(alu_1_r));
  Multiplexer #(.Bits(64)) multiplexer_5 (.sel(M2R), .in_0(alu_1_r), .in_1(load_unit_1_dcur), .out(multiplexer_5_out));
  store_unit store_unit_1 (
    .ADDR(alu_1_r), .RD1(register_file_1_rd1), .Dcur(Dcur), .sz(TYPE_OF_STORE_LOAD), .D(store_unit_1_d));
  RAMDualPort #(.AddrBits(7), .Bits(64)) ramdualport_1 (
    .A(alu_1_r[9:3]), .Din(store_unit_1_d), .str(ST), .C(CLK_t), .ld(LD), .D(Dcur));
  load_unit load_unit_1 (.ADDR(alu_1_r), .D64(Dcur), .MSZ(TYPE_OF_STORE_LOAD), .Dcur(load_unit_1_dcur));

  // Other names for the same wires on the sheet: MSZ[1:0] = TYPE_OF_STORE_LOAD; x0[63:0] = zero; x1[63:0] = ra;
  //   x2[63:0] = sp; x3[63:0] = gp; x4[63:0] = tp; x5[63:0] = T0; x6[63:0] = T1; x7[63:0] = T2; x8[63:0] = s0_fp;
  //   x9[63:0] = s1; x10[63:0] = A0; x11[63:0] = A1; x12[63:0] = A2; x13[63:0] = A3; x14[63:0] = A4; x15[63:0] = A5;
  //   x16[63:0] = A6; x17[63:0] = A7; x18[63:0] = s2; x19[63:0] = s3; x20[63:0] = s4; x21[63:0] = s5; x22[63:0] = s6;
  //   x23[63:0] = s7; x24[63:0] = s8; x25[63:0] = s9; x26[63:0] = s10; x27[63:0] = s11; x28[63:0] = T3;
  //   x29[63:0] = T4; x30[63:0] = T5; x31[63:0] = T6

  // Notes on the sheet:
  //   CLK: Hz: 2
endmodule

/* Test case 00-add-r-test:
CLR EN CLK PROG A2
1   0   0   x    x
0   0   0   x    x
while (!(DONE))
0   1   C   0    x
end while
0   1   0   0    3
*/

/* Test case 04-srl-r-test:
CLR EN CLK PROG A0
1   0   0   x    x
0   0   0   x    x
while (!(DONE))
0   1   C   4    x
end while
0   1   0   4    4
*/

/* Test case 08-jal-test:
EN CLR CLK PROG A0
1  1   0   x    x
1  0   0   x    x
while (!(DONE))
1  0   C   8    x
end while
1  0   0   8    3
*/

/* Test case 12-bge-test:
EN CLR CLK PROG A0
1  1   0   x    x
1  0   0   x    x
while (!(DONE))
1  0   C   12   x
end while
1  0   0   12   2
*/

/* Test case 16-quadratic-test:
CLR EN CLK PROG A0
1   0   0   x    x
0   0   0   x    x
while (!(DONE))
0   1   C   16    x
end while
0   1   0   16    25
*/

/* Test case 20-is-pal-test:
CLR EN CLK PROG A0
1   0   0   x    x
0   0   0   x    x
while (!(DONE))
0   1   C   20   x
end while
0   1   0   20   1
*/

/* Test case 01-add-i-test:
CLR EN CLK PROG A2
1   0   0   x    x
0   0   0   x    x
while (!(DONE))
0   1   C   1    x
end while
0   1   1   1    3
*/

/* Test case 05-srl-i-test:
CLR EN CLK PROG A0
1   0   0   x    x
0   0   0   x    x
while (!(DONE))
0   1   C   5    x
end while
0   1   0   5    8
*/

/* Test case 09-j-test:
EN CLR CLK PROG A0
1  1   0   x    x
1  0   0   x    x
while (!(DONE))
1  0   C   9    x
end while
1  0   0   9    1
*/

/* Test case 13-mul-test:
EN CLR CLK PROG A0
1  1   0   x    x
1  0   0   x    x
while (!(DONE))
1  0   C   13   x
end while
1  0   0   13   9
*/

/* Test case 17-get-bitseq-test:
CLR EN CLK PROG A0
1   0   0   x    x
0   0   0   x    x
while (!(DONE))
0   1   C   17   x
end while
0   1   0   17   6
*/

/* Test case 21-to-upper-test:
CLR EN CLK PROG A0
1   0   0   x    x
0   0   0   x    x
while (!(DONE))
0   1   C   21   x
end while
0   1   0   21   5066355251797426176
*/

/* Test case 02-sll-r-test:
CLR EN CLK PROG A0
1   0   0   x    x
0   0   0   x    x
while (!(DONE))
0   1   C   2    x
end while
0   1   0   2    4
*/

/* Test case 06-sd-ld-test:
CLR EN CLK PROG A0
1   0   0   x    x
0   0   0   x    x
while (!(DONE))
0   1   C   6    x
end while
0   1   0   6    99
*/

/* Test case 10-beq-test:
EN CLR CLK PROG A0
1  1   0   x    x
1  0   0   x    x
while (!(DONE))
1  0   C   10   x
end while
1  0   0   10   1
*/

/* Test case 14-lui-test:
EN CLR CLK PROG A0
1  1   0   x    x
1  0   0   x    x
while (!(DONE))
1  0   C   14   x
end while
1  0   0   14   4096
*/

/* Test case 18-max3-test:
CLR EN CLK PROG A0
1   0   0   x    x
0   0   0   x    x
while (!(DONE))
0   1   C   18   x
end while
0   1   0   18   2
*/

/* Test case 22-sort-test:
CLR EN CLK PROG A0 A1 A2
1   0   0   x    x    x    x
0   0   0   x    x    x    x
while (!(DONE))
0   1   C   22   x    x    x
end while
0   1   0   22   51539607562 34359738374 17179869186
*/

/* Test case 03-sll-i-test:
CLR EN CLK PROG A0
1   0   0   x    x
0   0   0   x    x
while (!(DONE))
0   1   C   3    x
end while
0   1   0   3    8
*/

/* Test case 07-sw-lw-test:
CLR EN CLK PROG A0
1   0   0   x    x
0   0   0   x    x
while (!(DONE))
0   1   C   7    x
end while
0   1   0   7    99
*/

/* Test case 11-blt-test:
EN CLR CLK PROG A0
1  1   0   x    x
1  0   0   x    x
while (!(DONE))
1  0   C   11   x
end while
1  0   0   11   1
*/

/* Test case 15-sb-lb-test:
CLR EN CLK PROG A0
1   0   0   x    x
0   0   0   x    x
while (!(DONE))
0   1   C   15    x
end while
0   1   0   15    99
*/

/* Test case 19-fib-rec-test:
CLR EN CLK PROG A0
1   0   0   x    x
0   0   0   x    x
while (!(DONE))
0   1   C   19   x
end while
0   1   0   19   55
*/

/* Test case 23-merge-sort-test:
CLR EN CLK PROG A0 A1 A2
1   0   0   x    x    x    x
0   0   0   x    x    x    x
while (!(DONE))
0   1   C   23   x    x    x
end while
0   1   0   23   8589934596 25769803784 42949672972
*/
