// Digital circuit register-file.dig as structural Verilog
module register_file (
  input  [4:0] RR0,
  input  [4:0] RR1,
  input  [4:0] WR,
  input  [63:0] WD,
  input  WE,
  input  CLR,
  input  CLK,
  output [63:0] RD0,
  output [63:0] RD1,
  output [63:0] x0,
  output [63:0] x1,
  output [63:0] x2,
  output [63:0] x3,
  output [63:0] x4,
  output [63:0] x5,
  output [63:0] x7,
  output [63:0] x8,
  output [63:0] x9,
  output [63:0] x10,
  output [63:0] x11,
  output [63:0] x6,
  output [63:0] x13,
  output [63:0] x14,
  output [63:0] x15,
  output [63:0] x16,
  output [63:0] x17,
  output [63:0] x12,
  output [63:0] x19,
  output [63:0] x20,
  output [63:0] x21,
  output [63:0] x22,
  output [63:0] x23,
  output [63:0] x18,
  output [63:0] x25,
  output [63:0] x26,
  output [63:0] x27,
  output [63:0] x28,
  output [63:0] x29,
  output [63:0] x24,
  output [63:0] x31,
  output [63:0] x30
);

  wire decoder_1_out_0, decoder_1_out_1, decoder_1_out_2, decoder_1_out_3, decoder_1_out_4, decoder_1_out_5,
       decoder_1_out_6, decoder_1_out_7, decoder_1_out_8, decoder_1_out_9, decoder_1_out_10,
       decoder_1_out_11, decoder_1_out_12, decoder_1_out_13, decoder_1_out_14, decoder_1_out_15,
       decoder_1_out_16, decoder_1_out_17, decoder_1_out_18, decoder_1_out_19, decoder_1_out_20,
       decoder_1_out_21, decoder_1_out_22, decoder_1_out_23, decoder_1_out_24, decoder_1_out_25,
       decoder_1_out_26, decoder_1_out_27, decoder_1_out_28, decoder_1_out_29, decoder_1_out_30,
       decoder_1_out_31;
  wire [4:0] multiplexer_1_out;

  Multiplexer #(.Bits(5)) multiplexer_1 (.sel(WE), .in_0({5{1'b0}}), .in_1(WR), .out(multiplexer_1_out));
  Decoder #(.Selector_Bits(5)) decoder_1 (
    .sel(multiplexer_1_out), .out_0(decoder_1_out_0), .out_1(decoder_1_out_1), .out_2(decoder_1_out_2),
    .out_3(decoder_1_out_3), .out_4(decoder_1_out_4), .out_5(decoder_1_out_5), .out_6(decoder_1_out_6),
    .out_7(decoder_1_out_7), .out_8(decoder_1_out_8), .out_9(decoder_1_out_9), .out_10(decoder_1_out_10),
    .out_11(decoder_1_out_11), .out_12(decoder_1_out_12), .out_13(decoder_1_out_13),
    .out_14(decoder_1_out_14), .out_15(decoder_1_out_15), .out_16(decoder_1_out_16),
    .out_17(decoder_1_out_17), .out_18(decoder_1_out_18), .out_19(decoder_1_out_19),
    .out_20(decoder_1_out_20), .out_21(decoder_1_out_21), .out_22(decoder_1_out_22),
    .out_23(decoder_1_out_23), .out_24(decoder_1_out_24), .out_25(decoder_1_out_25),
    .out_26(decoder_1_out_26), .out_27(decoder_1_out_27), .out_28(decoder_1_out_28),
    .out_29(decoder_1_out_29), .out_30(decoder_1_out_30), .out_31(decoder_1_out_31));
  _64_bit_register_w_clr _64_bit_register_w_clr_1 (.D(WD), .CLK(CLK), .EN(decoder_1_out_1), .CLR(CLR), .Q(x1));
  _64_bit_register_w_clr _64_bit_register_w_clr_2 (.D(WD), .CLK(CLK), .EN(decoder_1_out_2), .CLR(CLR), .Q(x2));
  _64_bit_register_w_clr _64_bit_register_w_clr_3 (.D(WD), .CLK(CLK), .EN(decoder_1_out_3), .CLR(CLR), .Q(x3));
  _64_bit_register_w_clr _64_bit_register_w_clr_4 (.D(WD), .CLK(CLK), .EN(decoder_1_out_4), .CLR(CLR), .Q(x4));
  _64_bit_register_w_clr _64_bit_register_w_clr_5 (.D(WD), .CLK(CLK), .EN(decoder_1_out_5), .CLR(CLR), .Q(x5));
  _64_bit_register_w_clr _64_bit_register_w_clr_6 (.D(WD), .CLK(CLK), .EN(decoder_1_out_6), .CLR(CLR), .Q(x6));
  _64_bit_register_w_clr _64_bit_register_w_clr_7 (.D(WD), .CLK(CLK), .EN(decoder_1_out_7), .CLR(CLR), .Q(x7));
  _64_bit_register_w_clr _64_bit_register_w_clr_8 (.D(WD), .CLK(CLK), .EN(decoder_1_out_8), .CLR(CLR), .Q(x8));
  _64_bit_register_w_clr _64_bit_register_w_clr_9 (.D(WD), .CLK(CLK), .EN(decoder_1_out_9), .CLR(CLR), .Q(x9));
  _64_bit_register_w_clr _64_bit_register_w_clr_10 (.D(WD), .CLK(CLK), .EN(decoder_1_out_10), .CLR(CLR), .Q(x10));
  _64_bit_register_w_clr _64_bit_register_w_clr_11 (.D(WD), .CLK(CLK), .EN(decoder_1_out_11), .CLR(CLR), .Q(x11));
  _64_bit_register_w_clr _64_bit_register_w_clr_12 (.D(WD), .CLK(CLK), .EN(decoder_1_out_12), .CLR(CLR), .Q(x12));
  _64_bit_register_w_clr _64_bit_register_w_clr_13 (.D(WD), .CLK(CLK), .EN(decoder_1_out_13), .CLR(CLR), .Q(x13));
  _64_bit_register_w_clr _64_bit_register_w_clr_14 (.D(WD), .CLK(CLK), .EN(decoder_1_out_14), .CLR(CLR), .Q(x14));
  _64_bit_register_w_clr _64_bit_register_w_clr_15 (.D(WD), .CLK(CLK), .EN(decoder_1_out_15), .CLR(CLR), .Q(x15));
  _64_bit_register_w_clr _64_bit_register_w_clr_16 (.D(WD), .CLK(CLK), .EN(decoder_1_out_16), .CLR(CLR), .Q(x16));
  _64_bit_register_w_clr _64_bit_register_w_clr_17 (.D(WD), .CLK(CLK), .EN(decoder_1_out_17), .CLR(CLR), .Q(x17));
  _64_bit_register_w_clr _64_bit_register_w_clr_18 (.D(WD), .CLK(CLK), .EN(decoder_1_out_18), .CLR(CLR), .Q(x18));
  _64_bit_register_w_clr _64_bit_register_w_clr_19 (.D(WD), .CLK(CLK), .EN(decoder_1_out_19), .CLR(CLR), .Q(x19));
  _64_bit_register_w_clr _64_bit_register_w_clr_20 (.D(WD), .CLK(CLK), .EN(decoder_1_out_20), .CLR(CLR), .Q(x20));
  _64_bit_register_w_clr _64_bit_register_w_clr_21 (.D(WD), .CLK(CLK), .EN(decoder_1_out_21), .CLR(CLR), .Q(x21));
  _64_bit_register_w_clr _64_bit_register_w_clr_22 (.D(WD), .CLK(CLK), .EN(decoder_1_out_22), .CLR(CLR), .Q(x22));
  _64_bit_register_w_clr _64_bit_register_w_clr_23 (.D(WD), .CLK(CLK), .EN(decoder_1_out_23), .CLR(CLR), .Q(x23));
  _64_bit_register_w_clr _64_bit_register_w_clr_24 (.D(WD), .CLK(CLK), .EN(decoder_1_out_24), .CLR(CLR), .Q(x24));
  _64_bit_register_w_clr _64_bit_register_w_clr_25 (.D(WD), .CLK(CLK), .EN(decoder_1_out_25), .CLR(CLR), .Q(x25));
  _64_bit_register_w_clr _64_bit_register_w_clr_26 (.D(WD), .CLK(CLK), .EN(decoder_1_out_26), .CLR(CLR), .Q(x26));
  _64_bit_register_w_clr _64_bit_register_w_clr_27 (.D(WD), .CLK(CLK), .EN(decoder_1_out_27), .CLR(CLR), .Q(x27));
  _64_bit_register_w_clr _64_bit_register_w_clr_28 (.D(WD), .CLK(CLK), .EN(decoder_1_out_28), .CLR(CLR), .Q(x28));
  _64_bit_register_w_clr _64_bit_register_w_clr_29 (.D(WD), .CLK(CLK), .EN(decoder_1_out_29), .CLR(CLR), .Q(x29));
  _64_bit_register_w_clr _64_bit_register_w_clr_30 (.D(WD), .CLK(CLK), .EN(decoder_1_out_30), .CLR(CLR), .Q(x30));
  _64_bit_register_w_clr _64_bit_register_w_clr_31 (.D(WD), .CLK(CLK), .EN(decoder_1_out_31), .CLR(CLR), .Q(x31));
  Multiplexer #(.Selector_Bits(5), .Bits(64)) multiplexer_2 (
    .sel(RR0), .in_0({64{1'b0}}), .in_1(x1), .in_2(x2), .in_3(x3), .in_4(x4), .in_5(x5), .in_6(x6),
    .in_7(x7), .in_8(x8), .in_9(x9), .in_10(x10), .in_11(x11), .in_12(x12), .in_13(x13), .in_14(x14),
    .in_15(x15), .in_16(x16), .in_17(x17), .in_18(x18), .in_19(x19), .in_20(x20), .in_21(x21), .in_22(x22),
    .in_23(x23), .in_24(x24), .in_25(x25), .in_26(x26), .in_27(x27), .in_28(x28), .in_29(x29), .in_30(x30),
    .in_31(x31), .out(RD0));
  Multiplexer #(.Selector_Bits(5), .Bits(64)) multiplexer_3 (
    .sel(RR1), .in_0({64{1'b0}}), .in_1(x1), .in_2(x2), .in_3(x3), .in_4(x4), .in_5(x5), .in_6(x6),
    .in_7(x7), .in_8(x8), .in_9(x9), .in_10(x10), .in_11(x11), .in_12(x12), .in_13(x13), .in_14(x14),
    .in_15(x15), .in_16(x16), .in_17(x17), .in_18(x18), .in_19(x19), .in_20(x20), .in_21(x21), .in_22(x22),
    .in_23(x23), .in_24(x24), .in_25(x25), .in_26(x26), .in_27(x27), .in_28(x28), .in_29(x29), .in_30(x30),
    .in_31(x31), .out(RD1));

  assign x0 = {64{1'b0}};

  // Other names for the same wires on the sheet: andrew[4:0] = RR1; jackson[4:0] = RR0; jefferson = CLR; thomas = CLK
endmodule
