// Digital circuit store-unit.dig as structural Verilog
module store_unit (
  input  [63:0] ADDR,
  input  [63:0] RD1,
  input  [63:0] Dcur,
  input  [1:0] sz,
  output [63:0] D
);

  wire [63:0] multiplexer_1_out, multiplexer_2_out;

  Multiplexer #(.Selector_Bits(3), .Bits(64)) multiplexer_1 (
    .sel(ADDR[2:0]), .in_0({Dcur[63:8], RD1[7:0]}), .in_1({Dcur[63:16], RD1[7:0], Dcur[7:0]}),
    .in_2({Dcur[63:24], RD1[7:0], Dcur[15:0]}), .in_3({Dcur[63:32], RD1[7:0], Dcur[23:0]}),
    .in_4({Dcur[63:40], RD1[7:0], Dcur[31:0]}), .in_5({Dcur[63:48], RD1[7:0], Dcur[39:0]}),
    .in_6({Dcur[63:56], RD1[7:0], Dcur[47:0]}), .in_7({RD1[7:0], Dcur[55:0]}), .out(multiplexer_1_out));
  Multiplexer #(.Bits(64)) multiplexer_2 (
    .sel(ADDR[2]), .in_0({Dcur[63:32], RD1[31:0]}), .in_1({RD1[31:0], Dcur[31:0]}), .out(multiplexer_2_out));
  Multiplexer #(.Selector_Bits(2), .Bits(64)) multiplexer_3 (
    .sel(sz), .in_0(multiplexer_1_out), .in_1({64{1'b0}}), .in_2(multiplexer_2_out), .in_3(RD1), .out(D));

  // Other names for the same wires on the sheet: b0[7:0] = Dcur[7:0]; d1[63:0] = {Dcur[63:16], RD1[7:0], Dcur[7:0]};
  //   d2[63:0] = {Dcur[63:24], RD1[7:0], Dcur[15:0]}; d3[63:0] = {Dcur[63:32], RD1[7:0], Dcur[23:0]};
  //   d4[63:0] = {Dcur[63:40], RD1[7:0], Dcur[31:0]}; d5[63:0] = {Dcur[63:48], RD1[7:0], Dcur[39:0]};
  //   d6[63:0] = {Dcur[63:56], RD1[7:0], Dcur[47:0]}; d7[63:0] = {RD1[7:0], Dcur[55:0]}; w0[31:0] = Dcur[31:0];
  //   b1[7:0] = Dcur[15:8]; d0[63:0] = {Dcur[63:8], RD1[7:0]}; b2[7:0] = Dcur[23:16]; b3[7:0] = Dcur[31:24];
  //   b4[7:0] = Dcur[39:32]; w1[31:0] = Dcur[63:32]; b5[7:0] = Dcur[47:40]; b6[7:0] = Dcur[55:48];
  //   b7[7:0] = Dcur[63:56]; bn0[7:0] = RD1[7:0]; wn[31:0] = RD1[31:0]
endmodule
